// Logisim project display.circ as structural Verilog
module display_7_seguimentos (
  input  a,
  input  b,
  input  c,
  input  d,
  output S5,
  output S6,
  output S0,
  output S1,
  output S2,
  output S3,
  output S4
);

  wire and_1_out, and_2_out, and_3_out, and_4_out, and_5_out, and_6_out, and_7_out, and_8_out, not_1_out,
       not_2_out, not_3_out, not_4_out, not_5_out, not_6_out, not_7_out, not_8_out;

  not not_1 (not_1_out, b);
  and and_1 (and_1_out, not_1_out, not_2_out);
  and and_2 (and_2_out, b, d);
  or or_1 (S0, a, c, and_1_out, and_2_out);
  not not_2 (not_2_out, d);
  or or_2 (S1, not_4_out, and_3_out, and_4_out);
  not not_3 (not_3_out, d);
  not not_4 (not_4_out, b);
  not not_5 (not_5_out, c);
  and and_3 (and_3_out, not_5_out, not_3_out);
  or or_3 (S2, not_6_out, b, d);
  not not_6 (not_6_out, c);
  and and_4 (and_4_out, c, d);
  and and_5 (and_5_out, c, not_7_out);
  or or_4 (S3, and_5_out, and_6_out, and_7_out, and_8_out, a);
  not not_7 (not_7_out, d);
  not not_8 (not_8_out, b);
  and and_6 (and_6_out, not_8_out, not_7_out);
  or or_5 (S4, and_5_out, and_6_out);
  and and_7 (and_7_out, not_8_out, c);
  and and_8 (and_8_out, not_8_out, d, b);
endmodule
